# Fritzing sketch Whole System Schematic (saved by Fritzing 0.9.3b)
breadboards: 1

parts:
  Part1 = Arduino Uno (Rev3)
  Part3 = Barometric Pressure Sensor - BMP085 Breakout
  J1 = Basic Force Sensing Resistor (FSR) [package=THT]
  part = Resistor [tolerance=±5% resistance=10k package="0805 [SMD]"]
  part_2 = Resistor [tolerance=±5% resistance=10k package="0805 [SMD]"]
  Part2 = IMU Digital Combo Board 6DOF
  part_3 = Resistor [tolerance=±5% resistance=10k package="0805 [SMD]"]
  Part4 = Arduino Uno (Rev3)
  J2 = Basic Servo
  J3 = Basic Servo
  SP1 = SPEAKER [package=pcb_mount_speaker]
  part_4 = Resistor [tolerance=±5% resistance=10k package="0805 [SMD]"]
  R3 = Resistor [tolerance=±5% resistance=10k package="0805 [SMD]"]
  R4 = Resistor [tolerance=±5% resistance=10k package="0805 [SMD]"]
  part_5 = Electrolytic Capacitor [capacitance=100μF package="0807 [SMD, electrolytic]"]
  C2 = Electrolytic Capacitor [capacitance=100μF package="0807 [SMD, electrolytic]"]
  C3 = Electrolytic Capacitor [capacitance=100μF package="0807 [SMD, electrolytic]"]
  J4 = Basic Servo
  J5 = Basic Servo
  J6 = Basic Servo
  J7 = Basic Servo
  Part5 = Arduino Uno (Rev3)
  Part6 = Arduino Color LCD Shield

nets:
  N1: Part1.A0, J1.pin_1, part_3.Pin_1
  N2: Part1.A4/SDA, Part3.SDA, part_2.Pin_0, Part2.SDA
  N3: Part1.D9_PWM, R4.Pin_0
  N4: Part1.D10_PWM/SS, R3.Pin_0
  N5: Part1.D11_PWM/MOSI, part_4.Pin_0
  GND: Part1.GND, Part3.GND, Part2.GND, part_3.Pin_0, Part4.GND, J2.gnd, J3.gnd, SP1.-, part_5.-, C2.-, C3.-, J4.gnd, J5.gnd, J6.gnd, J7.gnd, Part5.GND, Part6.GND
  N6: Part1.A5/SCL, Part3.SCL, part.Pin_0, Part2.SCL
  N7: Part1.D3_PWM, SP1.+
  N8: Part1.D5_PWM, J2.pulse
  N9: Part1.D6_PWM, J3.pulse
  5V: Part1.5V, J1.pin_0, Part4.5V, J2.vcc, J3.vcc, J4.vcc, J5.vcc, J6.vcc, J7.vcc, Part5.5V, Part6.5V
  3.3V: Part3.VCC, part.Pin_1, part_2.Pin_1, Part2.3.3V
  N10: Part4.A0, R4.Pin_1, part_5.+
  N11: Part4.A1, R3.Pin_1, C2.+
  N12: Part4.A2, part_4.Pin_1, C3.+
  N13: Part4.D9_PWM, J4.pulse
  N14: Part4.D10_PWM/SS, J5.pulse
  N15: Part4.D11_PWM/MOSI, J6.pulse
  N16: Part4.D12/MISO, J7.pulse
  N17: Part5.A0, Part6.A0
  N18: Part5.A1, Part6.A1
  N19: Part5.A2, Part6.A2
  N20: Part5.A3, Part6.A3
  N21: Part5.A4/SDA, Part6.A4
  N22: Part5.A5/SCL, Part6.A5
  N23: Part5.D8, Part6.D8
  N24: Part5.D9_PWM, Part6.D9
  N25: Part5.D10_PWM/SS, Part6.D10
  N26: Part5.D11_PWM/MOSI, Part6.D11
  N27: Part5.D12/MISO, Part6.D12
  N28: Part5.D13/SCK, Part6.D13
  N29: Part5.D0/RX, Part6.D0
  N30: Part5.D1/TX, Part6.D1
  N31: Part5.D2, Part6.D2
  N32: Part5.D3_PWM, Part6.D3
  N33: Part5.D4, Part6.D4
  N34: Part5.D5_PWM, Part6.D5
  N35: Part5.D6_PWM, Part6.D6
  N36: Part5.D7, Part6.D7
